# Fritzing sketch rhtlcd (saved by Fritzing 0.7.1b)
breadboards: 1

parts:
  Arduino = Arduino
  4_7kΩ_Resistor = Resistor [tolerance=±5% resistance=4.7 package=THT]
  RHT03 = Humidity and Temperature Sensor RHT03
  R4 = Rotary Potentiometer (Small) [maximum_resistance=100kΩ]
  220Ω_Resistor = Resistor [tolerance=±5% resistance=220 package=THT]
  LCD1 = LCD screen

nets:
  GND: Arduino.GND, RHT03.GND_2, R4.leg2, LCD1.VSS, LCD1.R/W, LCD1.LED+
  N1: Arduino.D12, LCD1.RS
  N2: Arduino.D11, LCD1.E
  N3: Arduino.D7, LCD1.DB4
  N4: Arduino.D6, LCD1.DB5
  N5: Arduino.D5, LCD1.DB6
  N6: Arduino.D4, LCD1.DB7
  N7: Arduino.D2, 4_7kΩ_Resistor.Pin_1, RHT03.Data-signal
  +5V: Arduino.+5V, 4_7kΩ_Resistor.Pin_0, RHT03.Vcc, R4.leg1, 220Ω_Resistor.Pin_0, LCD1.VDD
  N8: R4.wiper, LCD1.V0
  N9: 220Ω_Resistor.Pin_1, LCD1.LED-

notes:
  LCD Pins (from left)
  1: Ground
  2: 5V Power
  3: Contrast
  4: Register Select
  5: R/W (Grounded because we're always writing)
  6: Enable
  7-10: Data 0-3 (unused in 4 bit mode)
  11-14: Data 4-7 (4 bit mode)
  15: LED Power (220Ω to 5V, not sure why)
  16: LED Ground
  RHT03 Pins (from right)
  1: 5V Power
  2: Data (Digital) (4.7kΩ to 5V)
  3: Gnd (Unused)
  4: Gnd
